// Logisim project project.circ as structural Verilog: 5 circuits, main circuit main
module main (
  input  in_1,
  input  CLR,
  input  Clk,
  output [9:0] Read_Data_1,
  output [3:0] Opcode,
  output [1:0] RS,
  output [9:0] Read_Data_2,
  output [1:0] RT,
  output [1:0] RD_Imm,
  output [9:0] out_10,
  output [9:0] out_11,
  output [1:0] ALUOP,
  output [1:0] RD,
  output [1:0] RD_2,
  output [1:0] RD_3
);

  wire lw, Mem_Res, or_1_out, R_D, R_I, sw, WR;
  wire [1:0] multiplexer_1_out;
  wire [9:0] adder_1_out, bit_extender_1_out, multiplexer_2_out, ram_1_data, register_1_q, register_2_q,
       register_4_q, register_6_q, register_7_q, register_8_q, register_9_q, register_11_q, register_12_q,
       rom_1_data;

  Register #(.width(10)) register_1 (.D(register_2_q), .Q(register_1_q), .clk(Clk), .clr(CLR));  // open: en
  control_unit control_unit_1 (
    .in_1(Opcode), .RTorRD(R_D), .RW(WR), .RorI(R_I), .ALU__OP(ALUOP), .lw(lw), .sw(sw),
    .ResultorMemory(Mem_Res));
  Adder #(.width(10)) adder_1 (.a(register_1_q), .b(10'h1), .out(adder_1_out));  // open: cin, cout
  ROM #(.addrWidth(10), .dataWidth(10)) rom_1 (.addr(register_1_q), .data(rom_1_data));  // open: sel
  Register #(.width(10)) register_2 (.D(adder_1_out), .Q(register_2_q), .clk(Clk), .clr(CLR));  // open: en
  Register #(.width(10)) register_3 (.D(rom_1_data), .Q({Opcode, RS, RT, RD_Imm}), .clk(Clk), .clr(CLR));  // open: en
  Multiplexer #(.width(2)) multiplexer_1 (.in0(RD_Imm), .in1(RT), .out(multiplexer_1_out), .sel(R_D));  // open: en
  assign bit_extender_1_out = {{8{1'b0}}, RD_Imm};  // Bit_Extender bit_extender_1
  Regiser_file regiser_file_1 (
    .Data_IN(out_11), .Reg_Write(WR), .RD(RD), .Clock(Clk), .Data01(Read_Data_1), .Data02(Read_Data_2),
    .RS(RS), .RT(RT));  // open: in_2
  Register #(.width(10)) register_4 (.D(bit_extender_1_out), .Q(register_4_q), .clk(Clk), .clr(CLR));  // open: en
  Register #(.width(2)) register_5 (.D(multiplexer_1_out), .Q(RD_2), .clk(Clk), .clr(CLR));  // open: en
  Multiplexer #(.width(10)) multiplexer_2 (
    .in0(Read_Data_2), .in1(register_4_q), .out(multiplexer_2_out), .sel(R_I));  // open: en
  Register #(.width(10)) register_6 (.D(Read_Data_1), .Q(register_6_q), .clk(Clk), .clr(CLR));  // open: en
  _10_bit_ALU u_10_bit_alu_1 (
    .A(register_6_q), .B(register_7_q), .OP(ALUOP), .Cin(in_1), .Result(out_10));  // open: Overflow, Carry_Out, Zero_Signal
  Register #(.width(10)) register_7 (.D(multiplexer_2_out), .Q(register_7_q), .clk(Clk), .clr(CLR));  // open: en
  Register #(.width(10)) register_8 (.D(Read_Data_2), .Q(register_8_q), .clk(Clk), .clr(CLR));  // open: en
  Register #(.width(10)) register_9 (.D(out_10), .Q(register_9_q), .clk(Clk), .clr(CLR));  // open: en
  Register #(.width(2)) register_10 (.D(RD_2), .Q(RD_3), .clk(Clk));  // open: en, clr
  or or_1 (or_1_out, sw, lw);
  RAM #(.addrWidth(10), .dataWidth(10), .bus("separate")) ram_1 (
    .addr(register_9_q), .din(register_8_q), .data(ram_1_data), .str(sw), .sel(or_1_out), .clk(Clk), .ld(lw),
    .clr(CLR));
  Register #(.width(10)) register_11 (.D(out_10), .Q(register_11_q), .clk(Clk), .clr(CLR));  // open: en
  Register #(.width(10)) register_12 (.D(ram_1_data), .Q(register_12_q), .clk(Clk), .clr(CLR));  // open: en
  Register #(.width(2)) register_13 (.D(RD_3), .Q(RD), .clk(Clk), .clr(CLR));  // open: en
  Multiplexer #(.width(10)) multiplexer_3 (
    .in0(register_11_q), .in1(register_12_q), .out(out_11), .sel(Mem_Res));  // open: en

  // Other names for the same wires on the sheet: alu_op[1:0] = ALUOP

  // Notes on the sheet:
  //   contents of rom_1 (hex, n*v repeats v):
  //   6 72 b6 e4 106 152 1bb
endmodule

module Regiser_file (
  input  [9:0] Data_IN,
  input  in_2,
  input  Reg_Write,
  input  [1:0] RD,
  input  [1:0] RS,
  input  Clock,
  input  [1:0] RT,
  output [9:0] Data01,
  output [9:0] Data02
);

  wire demultiplexer_1_out0, demultiplexer_1_out1, demultiplexer_1_out2, demultiplexer_1_out3;
  wire [9:0] s1_q, s2_q, s3_q, s4_q;

  Demultiplexer #(.select(2)) demultiplexer_1 (
    .out0(demultiplexer_1_out0), .out1(demultiplexer_1_out1), .out2(demultiplexer_1_out2),
    .out3(demultiplexer_1_out3), .in(Reg_Write), .sel(RD));  // open: en
  Register #(.width(10)) s1 (.D(Data_IN), .en(demultiplexer_1_out0), .Q(s1_q), .clk(Clock), .clr(in_2));
  Register #(.width(10)) s2 (.D(Data_IN), .en(demultiplexer_1_out1), .Q(s2_q), .clk(Clock), .clr(in_2));
  Register #(.width(10)) s3 (.D(Data_IN), .en(demultiplexer_1_out2), .Q(s3_q), .clk(Clock), .clr(in_2));
  Register #(.width(10)) s4 (.D(Data_IN), .en(demultiplexer_1_out3), .Q(s4_q), .clk(Clock), .clr(in_2));
  Multiplexer #(.select(2), .width(10)) multiplexer_1 (
    .in0(s1_q), .in1(s2_q), .in2(s3_q), .in3(s4_q), .out(Data01), .sel(RS));  // open: en
  Multiplexer #(.select(2), .width(10)) multiplexer_2 (
    .in0(s1_q), .in1(s2_q), .in2(s3_q), .in3(s4_q), .out(Data02), .sel(RT));  // open: en
endmodule

module _1_bit_ALU (
  input  A,
  input  B,
  input  C_in,
  input  [1:0] ALU_Opcode,
  output Result,
  output Overflow,
  output Zero_Signal,
  output C_out
);

  wire adder_1_out, and_1_out, or_1_out, subtractor_1_out;

  and and_1 (and_1_out, A, B);
  or or_1 (or_1_out, A, B);
  Adder #(.width(1)) adder_1 (.a(A), .b(B), .out(adder_1_out), .cin(C_in), .cout(C_out));
  Subtractor #(.width(1)) subtractor_1 (.a(A), .b(B), .out(subtractor_1_out));  // open: bin, bout
  Multiplexer #(.select(2), .enable("false")) multiplexer_1 (
    .in0(and_1_out), .in1(or_1_out), .in2(adder_1_out), .in3(subtractor_1_out), .out(Result), .sel(ALU_Opcode));
  xor xor_1 (Overflow, Result, C_out);
  nor nor_1 (Zero_Signal, Result, C_out);
endmodule

module _10_bit_ALU (
  input  [1:0] OP,
  input  Cin,
  input  [9:0] A,
  input  [9:0] B,
  output Carry_Out,
  output [9:0] Result,
  output [9:0] Overflow,
  output [9:0] Zero_Signal
);

  wire n1_bit_alu_1_c_out, n1_bit_alu_2_c_out, n1_bit_alu_3_c_out, n1_bit_alu_4_c_out, n1_bit_alu_5_c_out,
       n1_bit_alu_6_c_out, n1_bit_alu_7_c_out, n1_bit_alu_8_c_out, n1_bit_alu_9_c_out;

  _1_bit_ALU u_1_bit_alu_1 (
    .Result(Result[0]), .Overflow(Overflow[0]), .Zero_Signal(Zero_Signal[0]), .C_out(n1_bit_alu_1_c_out),
    .A(A[0]), .B(B[0]), .C_in(Cin), .ALU_Opcode(OP));
  _1_bit_ALU u_1_bit_alu_2 (
    .Result(Result[1]), .Overflow(Overflow[1]), .Zero_Signal(Zero_Signal[1]), .C_out(n1_bit_alu_2_c_out),
    .A(A[1]), .B(B[1]), .C_in(n1_bit_alu_1_c_out), .ALU_Opcode(OP));
  _1_bit_ALU u_1_bit_alu_3 (
    .Result(Result[2]), .Overflow(Overflow[2]), .Zero_Signal(Zero_Signal[2]), .C_out(n1_bit_alu_3_c_out),
    .A(A[2]), .B(B[2]), .C_in(n1_bit_alu_2_c_out), .ALU_Opcode(OP));
  _1_bit_ALU u_1_bit_alu_4 (
    .Result(Result[3]), .Overflow(Overflow[3]), .Zero_Signal(Zero_Signal[3]), .C_out(n1_bit_alu_4_c_out),
    .A(A[3]), .B(B[3]), .C_in(n1_bit_alu_3_c_out), .ALU_Opcode(OP));
  _1_bit_ALU u_1_bit_alu_5 (
    .Result(Result[4]), .Overflow(Overflow[4]), .Zero_Signal(Zero_Signal[4]), .C_out(n1_bit_alu_5_c_out),
    .A(A[4]), .B(B[4]), .C_in(n1_bit_alu_4_c_out), .ALU_Opcode(OP));
  _1_bit_ALU u_1_bit_alu_6 (
    .Result(Result[5]), .Overflow(Overflow[5]), .Zero_Signal(Zero_Signal[5]), .C_out(n1_bit_alu_6_c_out),
    .A(A[5]), .B(B[5]), .C_in(n1_bit_alu_5_c_out), .ALU_Opcode(OP));
  _1_bit_ALU u_1_bit_alu_7 (
    .Result(Result[6]), .Overflow(Overflow[6]), .Zero_Signal(Zero_Signal[6]), .C_out(n1_bit_alu_7_c_out),
    .A(A[6]), .B(B[6]), .C_in(n1_bit_alu_6_c_out), .ALU_Opcode(OP));
  _1_bit_ALU u_1_bit_alu_8 (
    .Result(Result[7]), .Overflow(Overflow[7]), .Zero_Signal(Zero_Signal[7]), .C_out(n1_bit_alu_8_c_out),
    .A(A[7]), .B(B[7]), .C_in(n1_bit_alu_7_c_out), .ALU_Opcode(OP));
  _1_bit_ALU u_1_bit_alu_9 (
    .Result(Result[8]), .Overflow(Overflow[8]), .Zero_Signal(Zero_Signal[8]), .C_out(n1_bit_alu_9_c_out),
    .A(A[8]), .B(B[8]), .C_in(n1_bit_alu_8_c_out), .ALU_Opcode(OP));
  _1_bit_ALU u_1_bit_alu_10 (
    .Result(Result[9]), .Overflow(Overflow[9]), .Zero_Signal(Zero_Signal[9]), .C_out(Carry_Out), .A(A[9]),
    .B(B[9]), .C_in(n1_bit_alu_9_c_out), .ALU_Opcode(OP));
endmodule

module control_unit (
  input  [3:0] in_1,
  output RTorRD,
  output RW,
  output RorI,
  output [1:0] ALU__OP,
  output lw,
  output sw,
  output ResultorMemory
);

  wire not_1_out, not_2_out;

  not not_1 (not_1_out, in_1[2]);
  not not_2 (not_2_out, in_1[1]);
  or or_1 (RW, not_1_out, not_2_out);
  or or_2 (ALU__OP[1], in_1[1], in_1[2]);
  or or_3 (ALU__OP[0], in_1[0], in_1[2]);
  and and_1 (lw, in_1[2], in_1[0]);
  and and_2 (sw, in_1[2], in_1[1]);
  and and_3 (ResultorMemory, in_1[2], in_1[0]);

  assign RorI = in_1[2];
  assign RTorRD = in_1[2];
endmodule
